# Fritzing sketch dragon (saved by Fritzing 0.8.3b)
circuit board: 7.22485cm x 5.48921cm
breadboards: 1

parts:
  Part1 = Arduino Uno (Rev3)
  LED4 = RGB LED (com. anode, rbg) [part_number=Nose2 package="5 mm [THT]"]
  LED1 = RGB LED (com. anode, rbg) [part_number=Eye1 package="5 mm [THT]"]
  LED2 = RGB LED (com. anode, rbg) [part_number=Eye2 package="5 mm [THT]"]
  LED3 = RGB LED (com. anode, rbg) [part_number=Nose1 package="5 mm [THT]"]
  J4 = Basic Servo [part_number=EyebrowR]
  VCC3 = Battery block 9V
  S5 = Round Pushbutton [part_number="Push ButtonL"]
  J2 = Basic Servo [part_number=Ear]
  VCC4 = Battery block 6V [part_number=6v]
  J1 = Basic Servo [part_number=EyebrowL]
  U1 = SWITCH_SPDT [part_number=Switch package=kps-1290]
  Pad1 = Pad [width=6 height=6 connect=center]
  Pad2 = Pad [width=6 height=6 connect=center]
  Pad3 = Pad [width=6 height=6 connect=center]
  Pad4 = Pad [width=6 height=6 connect=center]
  Pad5 = Pad [width=5 height=5 connect=center]
  Pad7 = Pad [width=5 height=5 connect=center]
  Pad8 = Pad [width=5 height=5 connect=center]
  Pad10 = Pad [width=5 height=5 connect=center]
  Pad11 = Pad [width=5 height=5 connect=center]
  Pad12 = Pad [width=5 height=5 connect=center]
  Pad13 = Pad [width=5 height=5 connect=center]
  Pad14 = Pad [width=6 height=6 connect=center]  # not connected
  Pad15 = Pad [width=5 height=5 connect=center]
  Pad21 = Pad [width=5 height=5 connect=center]
  Pad23 = Pad [width=5 height=5 connect=center]
  Pad24 = Pad [width=5 height=5 connect=center]
  Pad25 = Pad [width=5 height=5 connect=center]
  Pad26 = Pad [width=5 height=5 connect=center]
  Pad28 = Pad [width=5 height=5 connect=center]
  Pad29 = Pad [width=5 height=5 connect=center]
  Pad31 = Pad [width=5 height=5 connect=center]
  Pad32 = Pad [width=5 height=5 connect=center]
  Pad33 = Pad [width=5 height=5 connect=center]
  Pad34 = Pad [width=5 height=5 connect=center]
  Pad35 = Pad [width=5 height=5 connect=center]  # not connected
  Pad36 = Pad [width=5 height=5 connect=center]  # not connected
  Pad37 = Pad [width=22.4977677777778 height=0.282222222222222 connect=center]  # not connected
  Pad39 = Pad [width=5 height=5 connect=center]
  Pad40 = Pad [width=5 height=5 connect=center]
  Pad41 = Pad [width=5 height=5 connect=center]
  Pad42 = Pad [width=5 height=5 connect=center]
  Pad43 = Pad [width=5 height=5 connect=center]
  Pad44 = Pad [width=5 height=5 connect=center]
  Pad45 = Pad [width=5 height=5 connect=center]
  Pad46 = Pad [width=5 height=5 connect=center]
  U2 = SWITCH_SPDT [part_number=Switch package=kps-1290]
  S6 = Round Pushbutton [part_number="Push ButtonR"]
  VCC5 = Battery block 6V [part_number="external power to charge"]

nets:
  N1: Part1.ICSP_MISO, Part1.D12/MISO, LED1.green_cathode, LED2.green_cathode
  N2: Part1.ICSP_MOSI, Part1.D11_PWM/MOSI, LED4.red_cathode, LED3.red_cathode
  GND: Part1.GND, LED4.common_anode, LED2.common_anode, LED3.common_anode, VCC3.-, J2.gnd, VCC4.-, J1.gnd, Pad1.pad, Pad2.pad, Pad3.pad, Pad4.pad, VCC5.-
  N3: Part1.D8, LED1.blue_cathode, LED2.blue_cathode
  N4: Part1.D10_PWM/SS, J2.pulse
  N5: Part1.D2, S5.leg0
  N6: Part1.D3_PWM, S6.leg0
  N7: Part1.D4, LED1.red_cathode, LED2.red_cathode
  N8: Part1.D5_PWM, J1.pulse
  N9: Part1.D6_PWM, J4.pulse
  N10: Part1.VIN, U2.S
  N11: LED1.common_anode, S5.leg1, S6.leg1
  VCC: J4.vcc, J2.vcc, J1.vcc, U1.O, VCC5.+
  N12: VCC3.+, U2.P
  N13: VCC4.+, U1.P
  N14: Pad5.pad, Pad7.pad
  N15: Pad8.pad, Pad10.pad
  N16: Pad11.pad, Pad21.pad
  N17: Pad12.pad, Pad13.pad, Pad15.pad
  N18: Pad23.pad, Pad24.pad
  N19: Pad25.pad, Pad26.pad
  N20: Pad28.pad, Pad32.pad
  N21: Pad29.pad, Pad31.pad
  N22: Pad33.pad, Pad34.pad
  N23: Pad39.pad, Pad40.pad
  N24: Pad41.pad, Pad42.pad
  N25: Pad43.pad, Pad44.pad
  N26: Pad45.pad, Pad46.pad

notes:
  Ground
  6V
  D3
  9V
  D10
  D4
  M
  D5
  D11
  D6
  D9

custom parts:
  Battery block 6V: Your standard 6 Volts battery block
